// Logisim project exo2.circ as structural Verilog: 2 circuits, main circuit main
module main (
  input  a,
  input  b,
  input  c,
  output x,
  output y
);

  circuit part_1 (.in_1(a), .in_2(b), .out_3(x));

  assign y = x;
endmodule

module circuit (
  input  in_1,
  input  in_2,
  output out_3
);

  wire and_1_out;

  or or_1 (out_3, ~in_1, and_1_out);  // OR_Gate
  and and_1 (and_1_out, in_1, in_2);
endmodule
